# Fritzing sketch megasorte (saved by Fritzing 0.9.0b)
breadboards: 1

parts:
  Arduino = Arduino Uno (Rev3)
  S1 = Pushbutton [package="[THT]"]
  S2 = Pushbutton [package="[THT]"]
  LCD1 = LCD screen
  R1 = Resistor [tolerance=±5% resistance=220 package=THT]
  R2 = Resistor [tolerance=±5% resistance=220 package=THT]

nets:
  N1: Arduino.D8, S1.Pin_3, S1.Pin_4, R2.Pin_0
  N2: Arduino.D9_PWM, S2.Pin_3, S2.Pin_4, R1.Pin_0
  N3: Arduino.D11_PWM/MOSI, LCD1.E
  N4: Arduino.D12/MISO, LCD1.RS
  GND: Arduino.GND, LCD1.VSS, LCD1.V0, LCD1.R/W, LCD1.LED-, R1.Pin_1, R2.Pin_1
  N5: Arduino.D2, LCD1.DB7
  N6: Arduino.D3_PWM, LCD1.DB6
  N7: Arduino.D4, LCD1.DB5
  N8: Arduino.D5_PWM, LCD1.DB4
  5V: Arduino.5V, S1.Pin_1, S1.Pin_2, S2.Pin_1, S2.Pin_2, LCD1.VDD, LCD1.LED+
